# Fritzing sketch rpi_drawing (saved by Fritzing 0.9.3b)

parts:
  Raspberry_Pi_1 = Raspberry Pi 3 [part_number=RPI-3-V1.2]
  Part1 = Triple Axis Accelerometer Breakout - ADXL345
  Part2 = Arduino Nano (Rev3.0) (ICSP)
  RGB_SMD_LED1 = SMD RGB LED (WS2812) [package=5050]
  RGB_SMD_LED2 = SMD RGB LED (WS2812) [package=5050]  # not connected

nets:
  3V3: Raspberry_Pi_1.3v3, Part1.VCC
  N1: Raspberry_Pi_1.GPIO2, Part1.SDA
  N2: Raspberry_Pi_1.GPIO3, Part1.SCL
  GND: Raspberry_Pi_1.GND, Part1.GND, Part2.GND, RGB_SMD_LED1.DOut
  N3: Raspberry_Pi_1.GIPO24, Part2.D5
  N4: Part2.D6, RGB_SMD_LED1.DIn
  5V: Part2.5V, RGB_SMD_LED1.VCC
